# Fritzing sketch HomeControlMonitor-Simple (saved by Fritzing 0.9.3b)
circuit board: 5cm x 4cm
breadboards: 1

parts:
  USB_Power_in = USB Connectors [package=usb-a-h]  # not connected
  C1 = Electrolytic Capacitor [capacitance=0.1mF package="100 mil [THT, electrolytic]"]
  C2 = Ceramic Capacitor [capacitance=100nF package="100 mil [THT, multilayer]"]
  J1 = female pin header, 2 pins [form="♀ (female)" part_number=Power]
  J3 = 1.44-128x128-SPI-TFT-display-ILI9163 [package=THT]
  J2 = female pin header, 2 pins [form="♀ (female)" part_number=SER]
  Adafruit_HUZZAH_ESP8266 = Adafruit HUZZAH ESP8266 Breakout [part_number=2471]

nets:
  GND: C1.-, C2.1, J1.pin2, J3.pin2, Adafruit_HUZZAH_ESP8266.GND
  5V: C1.+, C2.0, J1.pin1, J3.pin1, Adafruit_HUZZAH_ESP8266.VBat
  N1: J3.pin3, Adafruit_HUZZAH_ESP8266.#12
  3.3V: J3.pin4, J3.pin8, Adafruit_HUZZAH_ESP8266.3V
  N2: J3.pin5, Adafruit_HUZZAH_ESP8266.#16
  N3: J3.pin6, Adafruit_HUZZAH_ESP8266.#14
  N4: J3.pin7, Adafruit_HUZZAH_ESP8266.#13
  N5: J2.pin1, Adafruit_HUZZAH_ESP8266.RX
  N6: J2.pin2, Adafruit_HUZZAH_ESP8266.TX

notes:
  VCC in
  128x128 SPI TFT
  - +
  Home Controll Monitor, 1
  Vcc => 5V
  Gnd => Gnd
  CS => IO12
  RST => 3.3V
  A0 => IO16
  SDA => IO14
  SCK => IO13
  LED => 3.3V
  TX-RX

custom parts:
  1.44-128x128-SPI-TFT-display-ILI9163: 1.44" 128x128 TFT display SPI interface Controll chip ILI9163 8 Pin interface
