# Fritzing sketch HomeControlMonitor-Simple2 (saved by Fritzing 0.9.3b)
circuit board: 5.5cm x 3.5cm
breadboards: 1

parts:
  USB_Power_in = USB Connectors [package=usb-a-h]  # not connected
  C1 = Electrolytic Capacitor [capacitance=0.1mF package="100 mil [THT, electrolytic]"]
  C2 = Ceramic Capacitor [capacitance=100nF package="100 mil [THT, multilayer]"]
  J2 = female pin header, 2 pins [form="♀ (female)"]
  J1 = female pin header, 2 pins [form="♀ (female)"]
  J4 = female pin header, 2 pins [form="♀ (female)"]
  J3 = 1.44-128x128-SPI-TFT-display-ILI9163 [package=THT]
  J5 = female pin header, 8 pins [form="♀ (female)"]
  Adafruit_HUZZAH_ESP8266_Breakout1 = Adafruit HUZZAH ESP8266 Breakout [part_number=2471]

nets:
  GND: C1.-, C2.1, J1.pin2, J3.pin2, J5.pin2, Adafruit_HUZZAH_ESP8266_Breakout1.GND
  5V: C1.+, C2.0, J1.pin1, J3.pin1, J5.pin1, Adafruit_HUZZAH_ESP8266_Breakout1.VBat
  N1: J2.pin1, Adafruit_HUZZAH_ESP8266_Breakout1.RX
  N2: J2.pin2, Adafruit_HUZZAH_ESP8266_Breakout1.TX
  N3: J4.pin1, Adafruit_HUZZAH_ESP8266_Breakout1.#0
  N4: J4.pin2, Adafruit_HUZZAH_ESP8266_Breakout1.#2
  N5: J3.pin3, J5.pin3, Adafruit_HUZZAH_ESP8266_Breakout1.#12
  3.3V: J3.pin4, J3.pin8, J5.pin4, J5.pin8, Adafruit_HUZZAH_ESP8266_Breakout1.3V
  N6: J3.pin5, J5.pin5, Adafruit_HUZZAH_ESP8266_Breakout1.#16
  N7: J3.pin6, J5.pin6, Adafruit_HUZZAH_ESP8266_Breakout1.#14
  N8: J3.pin7, J5.pin7, Adafruit_HUZZAH_ESP8266_Breakout1.#13

notes:
  VCC in
  128x128 SPI TFT
  - +
  Home Controll Monitor, 1
  Vcc => 5V
  Gnd => Gnd
  CS => IO12
  RST => 3.3V
  A0 => IO16
  SDA => IO14
  SCK => IO13
  LED => 3.3V
  TX-RX
  0 2

custom parts:
  1.44-128x128-SPI-TFT-display-ILI9163: 1.44" 128x128 TFT display SPI interface Controll chip ILI9163 8 Pin interface
