# Fritzing sketch HomeControlMonitor (saved by Fritzing 0.9.3b)
circuit board: 5cm x 6cm
breadboards: 1

parts:
  USB_Power_in = USB Connectors [package=usb-a-h]  # not connected
  S2 = Adafruit TSL2561 [part_number=TSL2561 package="SIP (Single Inline) [THT]"]  # not connected
  C1 = Electrolytic Capacitor [capacitance=0.1mF package="100 mil [THT, electrolytic]"]
  C2 = Ceramic Capacitor [capacitance=100nF package="100 mil [THT, multilayer]"]
  S2_2 = Humidity and Temperature Sensor RHT03 [part_number=DHT11]  # not connected
  J1 = female pin header, 2 pins [form="♀ (female)" part_number=Power]
  J2 = female pin header, 4 pins [form="♀ (female)" part_number=TSL2561]
  J3 = female pin header, 3 pins [form="♀ (female)" part_number=DHT11]
  J4 = 1.44-128x128-SPI-TFT-display-ILI9163 [package=THT]
  Adafruit_HUZZAH_ESP8266_Breakout1 = Adafruit HUZZAH ESP8266 Breakout [part_number=2471]

nets:
  GND: C1.-, C2.1, J1.pin2, J2.pin2, J3.pin3, J4.pin2, Adafruit_HUZZAH_ESP8266_Breakout1.GND
  5V: C1.+, C2.0, J1.pin1, J2.pin1, J4.pin1, Adafruit_HUZZAH_ESP8266_Breakout1.VBat
  N1: J2.pin3, Adafruit_HUZZAH_ESP8266_Breakout1.#4
  N2: J2.pin4, Adafruit_HUZZAH_ESP8266_Breakout1.#5
  3.3V: J3.pin1, J4.pin4, J4.pin8, Adafruit_HUZZAH_ESP8266_Breakout1.3V
  N3: J3.pin2, Adafruit_HUZZAH_ESP8266_Breakout1.#2
  N4: J4.pin3, Adafruit_HUZZAH_ESP8266_Breakout1.#12
  N5: J4.pin5, Adafruit_HUZZAH_ESP8266_Breakout1.#16
  N6: J4.pin6, Adafruit_HUZZAH_ESP8266_Breakout1.#13
  N7: J4.pin7, Adafruit_HUZZAH_ESP8266_Breakout1.#14

notes:
  VCC in
  128x128 SPI TFT
  TSL2561
  DHT11
  - +
  Home Controll Monitor, 1

custom parts:
  Adafruit TSL2561: Adafruit TSL2561 Digital Luminosity/Lux/Light Sensor Breakout The TSL2561 luminosity sensor is an advanced digital light sensor, ideal for use in a wide range of light situations. Compared to low cost CdS cells, this sensor is more precise, allowing for exact lux calculations and can be configured for different gain/timing ranges to detect light ranges from up to 0.1 - 40,000+ Lux on the fly.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
  1.44-128x128-SPI-TFT-display-ILI9163: 1.44" 128x128 TFT display SPI interface Controll chip ILI9163 8 Pin interface
