# Fritzing sketch IR-AC (saved by Fritzing 0.9.2b)
circuit board: 3.5cm x 3.5cm
breadboards: 1

parts:
  R1 = Resistor [tolerance=±5% resistance=330 package=THT]
  LED1 = LED - 3mm [color="Infrared (850nm)" package="3 mm [THT]"]
  LED2 = LED - 3mm [color="Infrared (850nm)" package="3 mm [THT]"]
  Q1 = NPN-Transistor [part_number=S9014 package="TO92 [THT]"]
  I1 = HUZZAH ESP8266 Breakout
  USB_Power = Header 2 [package=jst-2-pth-ns]
  C1 = Ceramic Capacitor [capacitance=10nF package="100 mil [THT, multilayer]"]
  C2 = Electrolytic Capacitor [capacitance=10µF package="100 mil [THT, electrolytic]"]

nets:
  N1: R1.Pin_0, I1.GPIO13
  N2: R1.Pin_1, Q1.B
  N3: LED1.cathode, LED2.cathode, Q1.C
  5V: LED1.anode, LED2.anode, I1.VBAT, USB_Power.2, C1.1, C2.+
  GND: Q1.E, I1.GND, USB_Power.1, C1.0, C2.-
  N4: I1.RESET_5V, I1.GPIO16

notes:
  GND
  5V
  IR_RCV
  SER_CLK
  SER_STB
  SER_DIO
  with 3 buttons
  and IR receiver
  CT1628 board
  Power from USB charger

custom parts:
  HUZZAH ESP8266 Breakout: The ESP8266 processor from Espressif is an 80 MHz microcontroller with a full WiFi front-end (both as client and access point) and TCP/IP stack with DNS support as well.

// code stored in the sketch: IR-FujiDenzo.ino
/**
   Web controlled IR remote for FujiDenzo aircon

   Hardware
   Adafruit HUZZAH ESP8266 (ESP-12) module - https://www.adafruit.com/products/2471
   S9014 NPN transistor
   330 Ohm resistor
   2x IR led

   Receives commands for the aircon through WiFi.
   Checks production of solar panels
   Switch on/off the aircon depending on command or production of solar panels.

   @author Bernd Giesecke
   @version 0.1 beta December 2, 2015.
*/

/* Includes from libraties */
#include <Ticker.h>
#include <ESP8266WiFi.h>
#include <IRremoteESP8266.h>
#include <IRremoteInt.h>
#include <ArduinoJson.h>
#include <EEPROM.h>

#define AC_ID "fd1" // ID for aircon FujiDenzo in office room

/* wifiAPinfo.h contains wifi SSID and password */
/* file content looks like: */
/* Begin of file:
  const char* ssid = "YOUR_WIFI_SSID";
  const char* password = "YOUR_WIFI_PASSWORD";
   End of file */
#include "wifiAPinfo.h"

/** WiFiClient class to create TCP communication */
WiFiClient tcpClient;

/** WiFiServer class to create simple web server */
WiFiServer server(80);

/** IP address of this module */
IPAddress ipAddr(192, 168, 0, 142);
/** Gateway address of WiFi access point */
IPAddress ipGateWay(192, 168, 0, 1);
/** Network mask of the local lan */
IPAddress ipSubNet(255, 255, 255, 0);
/** IP address of this module */
IPAddress ipSPM(192, 168, 0, 140);

/** Received command (from lan or serial connection) */
int irCmd = 9999;
/** String to hold incoming command from serial port */
String inString = "";
/** Max number of commands for this aircon */
#define MAX_NUM_CMD 9

/** Mode status of aircon (only guess, as human could have used remote)
    acMode acTemp
    MSB ... LSB (2x8bit)
    xatp mmff xxtt tttt
    x = unused
    a = auto mode: 0 power control disabled
                   1 power control enabled 
    t = timer: 0 normal mode
               1 timer button pressed
    p = status: 0 off
                1 on
    mm = mode: 00 fan
               01 dry
               10 cool
    ff = fan speed: 00 low
                    01 medium
                    10 high
    tttttt = temperature: 010000 16 deg C
                          010001 17 deg C
                          010010 18 deg C
                          010011 19 deg C
                          010100 20 deg C
                          010101 21 deg C
                          010110 22 deg C
                          010111 23 deg C
                          011000 24 deg C
                          011001 25 deg C
                          011010 26 deg C
                          011011 27 deg C
                          011100 28 deg C
                          011101 29 deg C
                          011110 30 deg C
                          011111 31 deg C
                          100000 32 deg C
*/
byte acMode =     B11000000;
byte acTemp =     B00000000;
#define AUTO_OFF  B00000000
#define AUTO_ON   B01000000
#define AUTO_CLR  B10111111
#define AUTO_MASK B01000000
#define AUTO_ON   B01000000
#define TIM_OFF   B00000000
#define TIM_ON    B00100000
#define TIM_CLR   B11011111
#define TIM_MASK  B00100000
#define AC_OFF    B00000000
#define AC_ON     B00010000
#define AC_CLR    B11101111
#define AC_MASK   B00010000
#define MODE_FAN  B00000000
#define MODE_DRY  B00000100
#define MODE_COOL B00001000
#define MODE_CLR  B11110011
#define MODE_MASK B00001100
#define FAN_LOW   B00000000
#define FAN_MED   B00000001
#define FAN_HIGH  B00000010
#define FAN_CLR   B11111100
#define FAN_MASK  B00000011
#define TEMP_CLR  B11000000
#define TEMP_MASK B00111111

/** IR LED on GPIO13 for communciation with aircon */
#define IR_LED_OUT 13
/** Blue LED on GPIO2 for communication activities */
#define COM_LED 2
/** Red LED on GPIO2 for aircon control activities */
#define ACT_LED 0

/** Timer to contact spMonitor server to get current consumption */
Ticker getPowerTimer;
/** Flag for request to contact spMonitor server to get current consumption */
boolean powerUpdateTriggered = false;

/** Instance of the IR sender */
IRsend My_Sender(IR_LED_OUT);

/* Status of aircon related to power consumption value of the house
 * If consumption is negative => production higher than consumption => switch on aircon
 * If consumption is positive => production lower than consumption => switch off aircon
 * Tresholds: TODO adapt values
 *            positive => Switch aircon off = status 0
 *            -100W => Switch on aircon in fan mode low = status 1
 *            additional -50W => Switch aircon to fan mode medium = status 2
 *            additional -50W => Switch aircon to fan mode high = status 3
 *            additional -200W => Switch aircon to cool mode 25 deg C = status 4
 *            additional -200W => Switch aircon to cool mode 16 deg C = status 5
 * Check every minute to switch aircon on, if on, check every 5 minutes before changing to another level
 */
byte powerStatus = 0;
/** Power production value from spMonitor */
double solarPower = 0;
/** Power consumption of the house from spMonitor */
double consPower = 0;

/** Counter for "I am alive" red LED blinking in loop() */
long liveCnt = 0;

// code stored in the sketch: IR-FujiDenzo_0_Codes.ino
byte H_FAN[4] = {B00001000,B11100111,B01101000,B10010111};
byte M_FAN[4] = {B00001000,B11100111,B01110000,B10001111};
byte L_FAN[4] = {B00001000,B11100111,B01010000,B10101111};

byte COOL[4] =  {B00001000,B11100111,B00101000,B11010111};
byte DRY[4] =   {B00001000,B11100111,B00110000,B11001111};
byte FAN[4] =   {B00001000,B11100111,B00010000,B11101111};
byte POWER[4] = {B00001000,B11100111,B00000000,B11111111};

byte PLUS[4] =  {B00001000,B11100111,B10101000,B01010111};
byte MINUS[4] = {B00001000,B11100111,B10010000,B01101111};

byte TIMER[4] = {B00001000,B11100111,B10000000,B01111111};

unsigned int sendBuffer[67] = {9000,4500,450,700,450,700,450,700,450,700,450,1800,450,700,450,700,450,700,450,1800,450,1800,450,1800,450,700,450,700,450,1800,450,1800,450,1800,450,0,450,0,450,0,450,0,450,0,450,700,450,700,450,700,450,0,450,0,450,0,450,0,450,0,450,1800,450,1800,450,1800,450};

// code stored in the sketch: IR-FujiDenzo_1_Subs.ino
/**
   triggerGetPower
   called by Ticker getPowerTimer
   sets flag powerUpdateTriggered to true for handling in loop()
   will initiate a call to getPowerVal() from loop()
*/
void triggerGetPower() {
  powerUpdateTriggered = true;
}

/**
   sendCode
   Send IR command
*/
void sendCode(int repeat, unsigned int *rawCodes, int rawCount) {
  // Assume 38 KHz
  My_Sender.IRsend::sendRaw(rawCodes, rawCount, 38);
}

/**
   getVal
   Returns correct duration value depending on bit value
*/
unsigned int getVal(byte testVal, byte maskVal) {
  if ((testVal & maskVal) == maskVal) {
    return 1800;
  } else {
    return 700;
  }
}

/**
   buildBuffer
   Converts bit stream into IR command made of durations
*/
void buildBuffer(unsigned int *newBuffer, byte *cmd) {
  for (int i = 0; i < 4; i++) {
    newBuffer[(i * 16) + 3]  = getVal(cmd[i], B10000000);
    newBuffer[(i * 16) + 5]  = getVal(cmd[i], B01000000);
    newBuffer[(i * 16) + 7]  = getVal(cmd[i], B00100000);
    newBuffer[(i * 16) + 9]  = getVal(cmd[i], B00010000);
    newBuffer[(i * 16) + 11] = getVal(cmd[i], B00001000);
    newBuffer[(i * 16) + 13] = getVal(cmd[i], B00000100);
    newBuffer[(i * 16) + 15] = getVal(cmd[i], B00000010);
    newBuffer[(i * 16) + 17] = getVal(cmd[i], B00000001);
  }
}

/**
   sendCmd
   Prepares and sends IR command to aircon depending on
   requested command irCmd
*/
void sendCmd() {
  // Check validity of irCmd
  if (irCmd > 9) {
    Serial.println("Invalid command: " + String(irCmd));
    return;
  }

  digitalWrite(ACT_LED, LOW); // Switch on activity led

  byte lastTemp;
  switch (irCmd) {
    case 0: // H-Fan
      if ((acMode & AC_ON) == AC_ON) {
        acMode = acMode & FAN_CLR; // set fan bits to 0
        acMode = acMode | FAN_HIGH; // set mode bits to FAN HIGH mode
      }
      buildBuffer(&sendBuffer[0], &H_FAN[0]);
      break;
    case 1: // M-Fan
      if ((acMode & AC_ON) == AC_ON) {
        acMode = acMode & FAN_CLR; // set fan bits to 0
        acMode = acMode | FAN_MED; // set mode bits to FAN MEDIUM mode
      }
      buildBuffer(&sendBuffer[0], &M_FAN[0]);
      break;
    case 2: // L-Fan
      if ((acMode & AC_ON) == AC_ON) {
        acMode = acMode & FAN_CLR; // set fan bits to 0
        acMode = acMode | FAN_LOW; // set mode bits to FAN LOW mode
      }
      buildBuffer(&sendBuffer[0], &L_FAN[0]);
      break;
    case 3: // Cool
      if ((acMode & AC_ON) == AC_ON) {
        acMode = acMode & MODE_CLR; // set mode bits to 0
        acMode = acMode | MODE_COOL; // set mode bits to COOL mode
      }
      buildBuffer(&sendBuffer[0], &COOL[0]);
      break;
    case 4: // Dry
      if ((acMode & AC_ON) == AC_ON) {
        acMode = acMode & MODE_CLR; // set mode bits to 0
        acMode = acMode | MODE_DRY; // set mode bits to DRY mode
      }
      buildBuffer(&sendBuffer[0], &DRY[0]);
      break;
    case 5: // Fan
      if ((acMode & AC_ON) == AC_ON) {
        acMode = acMode & MODE_CLR; // set mode bits to 0
        acMode = acMode | MODE_FAN; // set mode bits to FAN mode
      }
      buildBuffer(&sendBuffer[0], &FAN[0]);
      break;
    case 6: // On-Off
      if ((acMode & AC_ON) == AC_ON) { // AC is on
        acMode = acMode & AC_CLR; // set power bit to 0
        acMode = acMode | AC_OFF;
      } else {
        acMode = acMode & AC_CLR; // set power bit to 0
        acMode = acMode | AC_ON;
      }
      buildBuffer(&sendBuffer[0], &POWER[0]);
      break;
    case 7: // Temp +
      if ((acMode & AC_ON) == AC_ON) {
        lastTemp = acTemp & TEMP_MASK;
        if (lastTemp < 32) {
          lastTemp++;
          acTemp = lastTemp;
        }
      }
      buildBuffer(&sendBuffer[0], &PLUS[0]);
      break;
    case 8: // Temp -
      if ((acMode & AC_ON) == AC_ON) {
        lastTemp = acTemp & TEMP_MASK;
        if (lastTemp > 0) {
          lastTemp--;
          acTemp = lastTemp;
        }
      }
      buildBuffer(&sendBuffer[0], &MINUS[0]);
      break;
    case 9: // Timer
      if ((acMode & AC_ON) == AC_ON) {
        if ((acMode & TIM_ON) == TIM_ON) { // TIMER is on
          acMode = acMode & TIM_CLR; // set timer bit to 0
          acMode = acMode | TIM_OFF;
        } else {
          acMode = acMode & TIM_CLR; // set power bit to 0
          acMode = acMode | TIM_ON;
        }
      }
      buildBuffer(&sendBuffer[0], &TIMER[0]);
      break;
  }
  // Send the command
  sendCode(0, &sendBuffer[0], 67);

  // Reset irCmd
  irCmd = 9999;
  digitalWrite(ACT_LED, HIGH); // Switch off activity led
}

/**
   initAC
   Initialize aircon to fan mode, low fan speed, temperature 25 deg C
   Call this only once after power on and make sure aircon is off when
   ESP8266 is powered off!
   This will fail if aircon is already on and there is no (easy) way
   to detect if the aircon is already on
*/
void initAC() {
  digitalWrite(ACT_LED, LOW); // Switch on activity led

  /* FIRST: switch on AC */
  acMode = acMode & AC_CLR; // set power bit to 0
  acMode = acMode | AC_ON;
  buildBuffer(&sendBuffer[0], &POWER[0]);
  sendCode(0, &sendBuffer[0], 67);
  delay(2000); // Wait 2 seconds to make sure the aircon is on
  /* SECOND: switch to COOL mode */
  acMode = acMode & MODE_CLR; // set mode bits to 0
  acMode = acMode | MODE_COOL; // set mode bits to COOL mode
  buildBuffer(&sendBuffer[0], &COOL[0]);
  sendCode(0, &sendBuffer[0], 67);
  delay(1000); // Wait 1 second to make sure the aircon mode is switched
  /* THIRD: switch to LOW FAN speed */
  acMode = acMode & FAN_CLR; // set fan bits to 0
  acMode = acMode | FAN_LOW; // set mode bits to FAN LOW mode
  buildBuffer(&sendBuffer[0], &L_FAN[0]);
  sendCode(0, &sendBuffer[0], 67);
  delay(1000); // Wait 1 second to make sure the aircon mode is switched
  /* FORTH: set temperature to 25 deg Celsius */
  acTemp = acTemp & TEMP_CLR; // set temperature bits to 0
  acTemp = acTemp + 25; // set temperature bits to 25
  /* We do not know the temperature setting of the aircon
      therefor we first raise 17 times (to set 32 degrees)
      then we lower 7 times to get back to 25 degrees
  */
  for (int i = 0; i < 16; i++) {
    buildBuffer(&sendBuffer[0], &PLUS[0]);
    sendCode(0, &sendBuffer[0], 67);
    delay(1000); // Wait 1 second to make sure the aircon mode is switched
  }
  for (int i = 0; i < 7; i++) {
    buildBuffer(&sendBuffer[0], &MINUS[0]);
    sendCode(0, &sendBuffer[0], 67);
    delay(1000); // Wait 1 second to make sure the aircon mode is switched
  }
  /* FIFTH: switch to FAN mode */
  acMode = acMode & MODE_CLR; // set mode bits to 0
  acMode = acMode | MODE_FAN; // set mode bits to FAN mode
  buildBuffer(&sendBuffer[0], &FAN[0]);
  sendCode(0, &sendBuffer[0], 67);
  delay(1000); // Wait 1 second to make sure the aircon mode is switched
  /* SIXTH: switch AC off */
  acMode = acMode & AC_CLR; // set status bits to 0
  acMode = acMode | AC_OFF; // set status to aircon off
  buildBuffer(&sendBuffer[0], &POWER[0]);
  sendCode(0, &sendBuffer[0], 67);
  digitalWrite(ACT_LED, HIGH); // Switch off activity led
}

/**
   replyClient
   answer request on http server
   returns command to client
*/
void replyClient(WiFiClient httpClient) {
  digitalWrite(COM_LED, HIGH);
  boolean isValidCmd = false;
  int waitTimeOut = 0;
  DynamicJsonBuffer jsonBuffer;

  // Prepare json object for the response
  JsonObject& root = jsonBuffer.createObject();
  root["result"] = "fail";
  root["device"] = AC_ID;

  // Wait until the client sends some data
  while (!httpClient.available()) {
    delay(1);
    waitTimeOut++;
    if (waitTimeOut > 5000) { // If no response for 5 seconds return
      httpClient.flush();
      root["result"] = "timeout";
      httpClient.print("Timeout");
      root.printTo(httpClient);
      httpClient.stop();
      digitalWrite(COM_LED, LOW);
      return;
    }
  }

  // Read the first line of the request
  String req = httpClient.readStringUntil('\r');
  // Prepare the response
  String statResponse = "fail " + req;
  root["result"] = statResponse;
  statResponse = "Cannot recognize request: " + req + "\n";
  if (req.substring(4, 8) == "/?c=") { // command received
    httpClient.flush();
    statResponse = "";
    for (int i = 8; i < 10; i++) {
      if (req.substring(i, i + 1) == "0") {
        statResponse += req.substring(i, i + 1);
        isValidCmd = true;
      } else {
        if (req.substring(i, i + 1).toInt() >= 1 && req.substring(i, i + 1).toInt() <= 9) {
          statResponse += req.substring(i, i + 1);
          isValidCmd = true;
        } else {
          isValidCmd = false;
          break;
        }
      }
    }
    if (isValidCmd) {
      irCmd = statResponse.toInt();
      root["result"] = "success";
      if (irCmd <= MAX_NUM_CMD) { // Aircon command received
        switch (irCmd) {
          case 0:
            statResponse = "Switch to High Fan\n";
            root["cmd"] = 0;
            break;
          case 1:
            statResponse = "Switch to Medium Fan\n";
            root["cmd"] = 1;
            break;
          case 2:
            statResponse = "Switch to Low Fan\n";
            root["cmd"] = 2;
            break;
          case 3:
            statResponse = "Switch to Cool\n";
            root["cmd"] = 3;
            break;
          case 4:
            statResponse = "Switch to Dry\n";
            root["cmd"] = 4;
            break;
          case 5:
            statResponse = "Switch to Fan\n";
            root["cmd"] = 5;
            break;
          case 6:
            statResponse = "Switch aircon On/Off \n";
            root["cmd"] = 6;
            break;
          case 7:
            statResponse = "Temp +\n";
            root["cmd"] = 7;
            break;
          case 8:
            statResponse = "Temp -\n";
            root["cmd"] = 8;
            break;
          case 9:
            statResponse = "Switch to Timer\n";
            root["cmd"] = 9;
            break;
        }
      } else if (irCmd == 99) { // Command to stop auto control
        acMode = acMode & AUTO_CLR;
        acMode = acMode | AUTO_OFF;
        getPowerTimer.detach();
        statResponse = "Power consumption control off\n";
        root["cmd"] = 99;
      } else if (irCmd == 98) { // Command to (re)start auto control
        acMode = acMode & AUTO_CLR;
        acMode = acMode | AUTO_ON;
        getPowerTimer.attach(60, triggerGetPower);
        statResponse = "Power consumption control on\n";
        root["cmd"] = 98;
      } else {
        statResponse = "Invalid command number: " + req + "\n";
        root["result"] = "fail invalid cmd";
      }
    } else {
      statResponse = "fail invalid cmd: " + req + "\n";
      root["result"] = statResponse;
      statResponse = "Invalid command: " + req + "\n";
    }
  } else if (req.substring(4, 7) == "/?s") { // status request received
    root["result"] = "success";
    httpClient.flush();
    // Display status of aircon
    statResponse = "Saved status:\n";
    if ((acMode & AC_ON) == AC_ON) {
      statResponse += "AC is on\n";
      root["power"] = 1;
    } else {
      statResponse += "AC is off\n";
      root["power"] = 0;
    }
    byte testMode = acMode & MODE_MASK;
    if (testMode == MODE_FAN) {
      statResponse += "Fan mode\n";
      root["mode"] = 0;
    } else if (testMode == MODE_DRY) {
      statResponse += "Dry mode\n";
      root["mode"] = 1;
    } else if (testMode == MODE_COOL) {
      statResponse += "Cool mode\n";
      root["mode"] = 2;
    }
    testMode = acMode & FAN_MASK;
    if (testMode == FAN_LOW) {
      statResponse += "Low fan speed\n";
      root["speed"] = 0;
    } else if (testMode == FAN_MED) {
      statResponse += "Medium fan speed\n";
      root["speed"] = 1;
    } else if (testMode == FAN_HIGH) {
      statResponse += "High fan speed\n";
      root["speed"] = 2;
    }
    testMode = acTemp & TEMP_MASK;
    statResponse += "Selected temperature = " + String(testMode) + "C\n";
    root["temp"] = testMode;

    // Display power consumption and production values
    statResponse += "Current power consumption: ";
    statResponse += String(consPower, 2) + "W\n";
    root["cons"] = consPower;
    statResponse += "Current power production: ";
    statResponse += String(solarPower, 2) + "W\n";
    root["solar"] = solarPower;

    // Display power cycle status
    statResponse += "Current power cycle status: ";
    statResponse += String(powerStatus) + "\n";
    root["status"] = powerStatus;

    // Display status of auto control by power consumption
    if ((acMode & AUTO_ON) == AUTO_ON) {
      statResponse += "Power control enabled";
      root["auto"] = 1;
    } else {
      statResponse += "Power control disabled";
      root["auto"] = 0;
    }
  } else if (req.substring(4, 7) == "/?r") { // initialization request received
    initAC();
    statResponse = "Initialization done\n";
    root["result"] = "success";
  } else if (req.substring(4, 7) == "/?d") { // device identification requested
    statResponse = String(AC_ID) + "\n";
    root["result"] = "success";
    root["device"] = AC_ID;
  }
  httpClient.flush();
  // Send the response to the client
  httpClient.print(statResponse);
  root.printTo(httpClient);
  httpClient.stop();
  digitalWrite(COM_LED, LOW);
}

/**
   checkPower
   Uses the power production of the solar panel to switch on/to/off
   aircon in fan or cool mode
*/
void checkPower() {
  /** Check current status */
  switch (powerStatus) {
    case 0: // aircon is off, no overproduction
      // aircon should be off, but maybe user switched it on manually
      if ((acMode & AC_ON) != AC_ON) {
        if (consPower < -100) { // over production exceeds 100W
          Serial.print("Over production > 100W : ");
          Serial.print(consPower, 2);
          Serial.print("Solar production = ");
          Serial.println(solarPower, 2);
          Serial.println("Switching on AC in FAN mode");
          irCmd = 6; // Switch on aircon in FAN mode
          sendCmd();
          // Change time to check consumption to 5 minutes (5*60s = 300)
          getPowerTimer.detach();
          getPowerTimer.attach(300, triggerGetPower);
          powerStatus = 1;
        }
      }
      break;
    case 1: // aircon is in fan mode, over production was > 100W
      if (consPower < -400) { // over production exceeds 500W
        Serial.print("Over production > 500W : ");
        Serial.print(consPower, 2);
        Serial.print("Solar production = ");
        Serial.println(solarPower, 2);
        Serial.println("Switching on AC in COOL mode");
        irCmd = 3; // Switch aircon to COOL mode
        sendCmd();
        powerStatus = 2;
        // TODO: Send alarm to user to close doors and windows
      }
      if (consPower > 100) { // consuming more than 100W
        Serial.print("Consumption > 100W : ");
        Serial.print(consPower, 2);
        Serial.print("Solar production = ");
        Serial.println(solarPower, 2);
        Serial.println("Switching off AC");
        irCmd = 6; // Switch off aircon
        sendCmd();
        // Change time to check consumption back to 1 minutes
        getPowerTimer.detach();
        getPowerTimer.attach(60, triggerGetPower);
        powerStatus = 0;
      }
      break;
    case 2: // aircon is in cool mode, over production was > 500W
      if (consPower < -100) { // over production exceeds 600W
        // Switch on second aircon in FAN mode
        Serial.print("Over production > 600W : ");
        Serial.print(consPower, 2);
        Serial.print("Solar production = ");
        Serial.println(solarPower, 2);
        Serial.println("Switching on second AC in FAN mode");
        // TODO: Add communication to second aircon
        //powerStatus = 3;
      }
      if (consPower > 400) { // consuming more than 400W
        Serial.print("Consumption > 400W : ");
        Serial.print(consPower, 2);
        Serial.print("Solar production = ");
        Serial.println(solarPower, 2);
        Serial.println("Switching back to FAN mode");
        irCmd = 5; // Switch aircon to FAN mode
        sendCmd();
        powerStatus = 1;
      }
      break;
  }
}

/**
   getPowerVal
   Get current power consumption from spMonitor device on address ipSPM
*/
void getPowerVal(boolean doPowerCheck) {
  digitalWrite(COM_LED, HIGH);
  const int httpPort = 80;
  if (!tcpClient.connect(ipSPM, httpPort)) {
    Serial.println("connection to time server " + String(ipSPM[0]) + "." + String(ipSPM[1]) + "." + String(ipSPM[2]) + "." + String(ipSPM[3]) + " failed");
    tcpClient.stop();
    digitalWrite(COM_LED, LOW);
    return;
  }
  tcpClient.print("GET /data/get HTTP/1.0\r\n\r\n");

  // Read all the lines of the reply from server and print them to Serial
  String line = "";
  while (tcpClient.connected()) {
    line = tcpClient.readStringUntil('\r');
  }
  tcpClient.stop();
  /** Buffer for JSON string */
  DynamicJsonBuffer jsonBuffer;
  char json[line.length()];
  line.toCharArray(json, line.length() + 1);
  JsonObject& root = jsonBuffer.parseObject(json);
  if (!root.success()) {
    Serial.println("parseObject() failed");
    return;
  }

  // Switch between status depending on consumption
  solarPower = root["value"]["S"];
  consPower = root["value"]["C"];
  if (doPowerCheck) {
    checkPower();
  }
  digitalWrite(COM_LED, LOW);
}

// code stored in the sketch: IR-FujiDenzo_8_Setup.ino
void setup() {
  pinMode(IR_LED_OUT, OUTPUT); // IR LED red
  pinMode(COM_LED, OUTPUT); // Communication LED blue
  pinMode(ACT_LED, OUTPUT); // Communication LED blue
  digitalWrite(IR_LED_OUT, LOW); // Turn off IR LED
  digitalWrite(COM_LED, LOW); // Turn off LED
  digitalWrite(ACT_LED, HIGH); // Turn off LED

  Serial.begin(115200);

  Serial.setDebugOutput(false);
  Serial.println("");
  Serial.println("Hello from ESP8266");

  WiFi.mode(WIFI_STA);
  WiFi.config(ipAddr, ipGateWay, ipSubNet);
  WiFi.begin(ssid, password);
  Serial.print("Waiting for WiFi connection ");
  while (WiFi.status() != WL_CONNECTED) {
    delay(500);
    Serial.print(".");
  }
  Serial.println("");
  Serial.print("Connected to ");
  Serial.println(ssid);
  Serial.print("IP address: ");
  Serial.println(WiFi.localIP());

  // Start the web server to serve incoming requests
  server.begin();

  My_Sender.begin();

  Serial.println(F("0 - High Fan"));
  Serial.println(F("1 - Medium Fan"));
  Serial.println(F("2 - Low Fan"));
  Serial.println(F("3 - Cool"));
  Serial.println(F("4 - Dry"));
  Serial.println(F("5 - Fan"));
  Serial.println(F("6 - On/Off"));
  Serial.println(F("7 - Plus"));
  Serial.println(F("8 - Minus"));
  Serial.println(F("9 - Timer"));

  /* Asume aircon off, timer off, power control enabled, */
  /* aircon mode fan, fan speed low, temperature set to 25 deg Celsius */
  // TODO save status in EEPROM and read it from there after reboot
  acMode = acMode | AUTO_ON | TIM_OFF | AC_OFF | MODE_FAN | FAN_LOW;
  acTemp = acTemp & TEMP_CLR; // set temperature bits to 0
  acTemp = acTemp + 25; // set temperature bits to 25

  // Get first values from spMonitor
  getPowerVal(false);

  // Start update of consumption value every 60 seconds if enabled
  if ((acMode & AUTO_ON) == AUTO_ON) {
    getPowerTimer.attach(60, triggerGetPower);
  }

  // Initialize EEPROM access
  EEPROM.begin(512);

  // For debug, print out all EEPROM content
  //  byte value;
  //  int address_row;
  //  int address_col;
  //  for (int i = 0; i < 32; i++) {
  //    address_row = i * 16;
  //    Serial.print(address_row);
  //    Serial.print(":\t");
  //    for (int j = 0; j < 16; j++) {
  //      address_col = j + (i * 16);
  //      value = EEPROM.read(address_col);
  //      Serial.print(value, DEC);
  //      Serial.print(":");
  //    }
  //    Serial.print(" - ");
  //    for (int j = 0; j < 16; j++) {
  //      address_col = j + (i * 16);
  //      value = EEPROM.read(address_col);
  //      if (value > 32 && value < 128) {
  //        Serial.print(char(value));
  //        Serial.print(" ");
  //      } else {
  //        Serial.print(". ");
  //      }
  //    }
  //    Serial.println();
  //  }
}

// code stored in the sketch: IR-FujiDenzo_9_Loop.ino
void loop() {
  // Handle new client request on HTTP server if available
  WiFiClient client = server.available();
  if (client) {
    replyClient(client);
  }

  while (Serial.available() > 0) {
    digitalWrite(COM_LED, LOW);
    int inChar = Serial.read();
    if (isDigit(inChar)) {
      // convert the incoming byte to a char
      // and add it to the string:
      inString += (char)inChar;
    }
    // if you get a newline, print the string,
    // then the string's value:
    if (inChar == '\n') {
      irCmd = inString.toInt();
      if (irCmd > MAX_NUM_CMD) {
        Serial.println("Invalid command");
        irCmd = 9999;
      }
      // clear the string for new input:
      inString = "";
    }
  }
  digitalWrite(COM_LED, HIGH);

  if (powerUpdateTriggered) {
	Serial.println("Power Update triggered");
    powerUpdateTriggered = false;
    getPowerVal(true);
  }

  if (irCmd != 9999) {
	Serial.println("Send command triggered");
    sendCmd();
  }
  
  // Give a "I am alive" signal
  liveCnt++;
  if (liveCnt == 100000) {
    digitalWrite(ACT_LED,!digitalRead(ACT_LED));
  }
  if (liveCnt > 100000) {
    liveCnt = 0;
  }
}
