# Fritzing sketch Security-Simple-pcb (saved by Fritzing 0.9.2b)
circuit board: 8cm x 5.5cm
perfboards: 1

parts:
  USB_Power_in = USB Connectors [package=usb-a-h]
  Adafruit_PIR = PIR sensor
  Q1 = TRANSISTOR_NPN [package=to-92]
  R1 = Resistor [tolerance=±5% resistance=1k package=THT]
  Relay_DFR0017_V3_1 = RelayModule DFR0017 V3.1
  C1 = Electrolytic Capacitor [capacitance=0.1mF package="100 mil [THT, electrolytic]"]
  C2 = Ceramic Capacitor [capacitance=100nF package="100 mil [THT, multilayer]"]
  Adafruit_HUZZAH_ESP8266 = Adafruit HUZZAH ESP8266 Breakout [part_number=2471]
  Speaker = Piezo Speaker
  Q2 = TRANSISTOR_NPN [package=to-92]
  R2 = Resistor [tolerance=±5% resistance=1k package=THT]
  R3 = Resistor [tolerance=±5% resistance=1k package=THT]
  Q3 = TRANSISTOR_NPN [package=to-92]
  R4 = Resistor [tolerance=±5% resistance=1k package=THT]
  R5 = Resistor [tolerance=±5% resistance=1k package=THT]

nets:
  5V: USB_Power_in.VBUS, Adafruit_PIR.VDD, Relay_DFR0017_V3_1.5V, C1.+, C2.0, Adafruit_HUZZAH_ESP8266.VBat, Speaker.pin2, Q3.C
  GND: USB_Power_in.GND, Adafruit_PIR.GND, Q1.E, Relay_DFR0017_V3_1.GND, C1.-, C2.1, Adafruit_HUZZAH_ESP8266.GND, R3.Pin_0, R4.Pin_0
  N1: Adafruit_PIR.SIG, R2.Pin_1
  N2: Q1.B, R1.Pin_0
  Alarm_Spk: Q1.C, Speaker.pin1
  Alarm_Out: R1.Pin_1, Adafruit_HUZZAH_ESP8266.#15
  Relay_On: Relay_DFR0017_V3_1.SIGNAL, Q3.E, R4.Pin_1
  N3: Adafruit_HUZZAH_ESP8266.#16, Adafruit_HUZZAH_ESP8266.RST
  N4: Adafruit_HUZZAH_ESP8266.#5, R5.Pin_1
  PIR_Signal: Adafruit_HUZZAH_ESP8266.#4, Q2.E, R3.Pin_1
  3.3V: Adafruit_HUZZAH_ESP8266.3V, Q2.C
  N5: Q2.B, R2.Pin_0
  N6: Q3.B, R5.Pin_0

notes:
  ESP8266 backyard auto light, 1.0
  Relay
  GND
  5V
  SIG
  SND
  RST
  A
  16
  3.3V
  15
  5
  4
  +
  -
