# Fritzing sketch Security-backyard (saved by Fritzing 0.9.2b)
circuit board: 7cm x 2cm
circuit board: 7cm x 6cm
circuit board: 7cm x 1.5cm
breadboards: 1

parts:
  USB_Power_in = USB Connectors [package=usb-a-h]
  Adafruit_PIR = PIR sensor
  R1 = Resistor [tolerance=±20% resistance=1k package=THT]
  C1 = Electrolytic Capacitor [capacitance=0.1mF package="100 mil [THT, electrolytic]"]
  C2 = Ceramic Capacitor [capacitance=100nF package="100 mil [THT, multilayer]"]
  POWERe = male pin header, 2 pins [form="♂ (male)" part_number=Power2]
  DHT = female pin header, 3 pins [form="♀ (female)" part_number=DHT1]
  DHTe = male pin header, 3 pins [form="♂ (male)" part_number=DHT2]
  TSL = female pin header, 4 pins [form="♀ (female)" part_number=TSL1]
  TSLe = male pin header, 4 pins [form="♂ (male)" part_number=TSL2]
  PIRe = male pin header, 3 pins [form="♂ (male)" part_number=PIR2]
  PIR = female pin header, 3 pins [form="♀ (female)" part_number=PIR1]
  R2 = Resistor [tolerance=±5% resistance=1k package=THT]
  R3 = Resistor [tolerance=±5% resistance=1k package=THT]
  Adafruit_HUZZAH_ESP8266_Breakout = Adafruit HUZZAH ESP8266 Breakout [part_number=2471]
  POWER = female pin header, 2 pins [form="♀ (female)"]
  TSL2561 = Adafruit TSL2561 [package="SIP (Single Inline) [THT]"]
  DHT1 = DHT11 Humitidy and Temperature Sensor
  SPEAKER = Loudspeaker
  RELAY = RELAY MODULE - 10A - 1 CHANNEL [part_number=RELAY package=THT]
  Q2 = TRANSISTOR_NPN [package=to-92]
  Q1 = TRANSISTOR_NPN [package=to-92]
  IC1 = IC, DIP package, 8 pins [chip_label=CM6800C part_number=CM6800C]
  R4 = Resistor [tolerance=±5% resistance=22k package=THT]
  R5 = Resistor [tolerance=±20% resistance=22k package=THT]
  C4 = Electrolytic Capacitor [capacitance=1µF package="100 mil [THT, electrolytic]"]
  C3 = Ceramic Capacitor [capacitance=100nF package="200 mil [THT, multilayer]"]

nets:
  N1: USB_Power_in.VBUS, POWERe.pin2
  N2: USB_Power_in.GND, POWERe.pin1
  N3: Adafruit_PIR.VDD, PIRe.pin3
  N4: Adafruit_PIR.SIG, PIRe.pin2
  N5: Adafruit_PIR.GND, PIRe.pin1
  N6: R1.Pin_0, Q1.B
  N7: R1.Pin_1, Adafruit_HUZZAH_ESP8266_Breakout.#15
  GND: C1.-, C2.1, DHT.pin1, TSL.pin2, PIR.pin1, R3.Pin_1, Adafruit_HUZZAH_ESP8266_Breakout.GND, POWER.pin2, RELAY.pin2, IC1.pin1, IC1.pin7, C4.-
  5V: C1.+, C2.0, TSL.pin1, PIR.pin3, Adafruit_HUZZAH_ESP8266_Breakout.VBat, POWER.pin1, RELAY.pin1, Q2.C, Q1.C, IC1.pin6
  N8: DHT.pin2, Adafruit_HUZZAH_ESP8266_Breakout.#14
  3.3V: DHT.pin3, Adafruit_HUZZAH_ESP8266_Breakout.3V
  N9: DHTe.pin1, DHT1.GND
  N10: DHTe.pin2, DHT1.DATA
  N11: DHTe.pin3, DHT1.VDD
  N12: TSL.pin3, Adafruit_HUZZAH_ESP8266_Breakout.#13
  N13: TSL.pin4, Adafruit_HUZZAH_ESP8266_Breakout.#12
  N14: TSLe.pin1, TSL2561.SCL
  N15: TSLe.pin2, TSL2561.SDA
  N16: TSLe.pin3, TSL2561.GND
  N17: TSLe.pin4, TSL2561.Vin
  N18: PIR.pin2, Adafruit_HUZZAH_ESP8266_Breakout.#4
  N19: R2.Pin_0, Q2.B
  N20: R2.Pin_1, Adafruit_HUZZAH_ESP8266_Breakout.#5
  N21: R3.Pin_0, RELAY.pin3, Q2.E
  N22: Adafruit_HUZZAH_ESP8266_Breakout.#16, Adafruit_HUZZAH_ESP8266_Breakout.RST
  N23: SPEAKER.pin1, IC1.pin8
  N24: SPEAKER.pin2, IC1.pin5, R4.Pin_0
  N25: Q1.E, C3.0
  N26: IC1.pin2, IC1.pin3, C4.+
  N27: IC1.pin4, R4.Pin_1, R5.Pin_0
  N28: R5.Pin_1, C3.1

notes:
  Security Backyard, Motion detection and automatic light sensor, hymidity, temperature and light sensor, 1

custom parts:
  Adafruit TSL2561: Adafruit TSL2561 Digital Luminosity/Lux/Light Sensor Breakout The TSL2561 luminosity sensor is an advanced digital light sensor, ideal for use in a wide range of light situations. Compared to low cost CdS cells, this sensor is more precise, allowing for exact lux calculations and can be configured for different gain/timing ranges to detect light ranges from up to 0.1 - 40,000+ Lux on the fly.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
  DHT11 Humitidy and Temperature Sensor: DHT11 Humidity and Temperature Sensor
  RELAY MODULE - 10A - 1 CHANNEL: Control Voltage: 5V DC Max Control Capacity:10A@250VAC or 10A@30VDC
