# Fritzing sketch spMonitor (saved by Fritzing 0.9.2b)
circuit board: 3cm x 2.5cm
circuit board: 8.5cm x 10.5cm
circuit board: 7cm x 4cm
breadboards: 1

parts:
  Part1 = Arduino Yun [part_number="Arduino Yun"]
  R1 = Resistor [tolerance=±5% resistance=100k package=THT]
  R2 = Resistor [tolerance=±5% resistance=10k package=THT]
  C1 = Electrolytic Capacitor [capacitance=10µF package="100 mil [THT, electrolytic]"]
  R3 = Resistor [tolerance=±5% resistance=470k package=THT]
  R4 = Resistor [tolerance=±5% resistance=470k package=THT]
  R5 = Resistor [tolerance=±5% resistance=470k package=THT]
  R6 = Resistor [tolerance=±5% resistance=470k package=THT]
  C2 = Electrolytic Capacitor [capacitance=10µF package="100 mil [THT, electrolytic]"]
  R7 = Resistor [tolerance=±5% resistance=330 package=THT]
  R8 = Resistor [tolerance=±5% resistance=330 package=THT]
  R9 = Resistor [tolerance=±5% resistance=470k package=THT]
  R10 = Resistor [tolerance=±5% resistance=470k package=THT]
  C3 = Electrolytic Capacitor [capacitance=10µF package="100 mil [THT, electrolytic]"]
  R11 = Resistor [tolerance=±5% resistance=330 package=THT]
  JP1 = Header 4 [package=molex-1x4_lock]
  R12 = Resistor [tolerance=±5% resistance=1k package=THT]
  U1 = Transformer [package=transformer]
  U2 = Adafruit TSL2561 [package="SIP (Single Inline) [THT]"]
  JP2 = Header 4 [package=molex-1x4_lock]
  L2 = Inductor [package="400 mil [THT]"]
  TRS1 = Audio Jack (TRS) 3.5mm [package="PG203J [THT]"]
  TRS2 = Audio Jack (TRS) 3.5mm [package="PG203J [THT]"]
  TRS3 = Audio Jack (TRS) 3.5mm [package="PG203J [THT]"]
  L1 = Inductor [package="400 mil [THT]"]
  U3 = 2.5mm Audio Jack [package=stereojack2.5mm_stereojack2.5mm]
  U4 = 2.5mm Audio Jack [package=stereojack2.5mm_stereojack2.5mm]
  U5 = 2.5mm Audio Jack [package=stereojack2.5mm_stereojack2.5mm]
  JP3 = Header 2 [package=screwterminal-3.5mm-2_lock]
  LED1 = LED - 3mm [color="White (4500K)" package="3 mm [THT]"]

nets:
  N1: Part1.A0, R11.Pin_1, TRS3.Ring, TRS3.Tip
  N2: Part1.A1, R7.Pin_1, R8.Pin_1, TRS2.Ring, TRS2.Tip
  N3: Part1.A2, R1.Pin_0, R2.Pin_0
  5V: Part1.5V, R3.Pin_1, R6.Pin_1, R9.Pin_1, JP1.1
  N4: Part1.ICSP_SCK, Part1.D13/SCK, LED1.anode
  GND: Part1.GND, C1.-, R4.Pin_1, R5.Pin_1, C2.-, R10.Pin_1, C3.-, JP1.4, R12.Pin_0
  N5: Part1.D2/SDA, JP1.2
  N6: Part1.D3/SCL, JP1.3
  N7: R1.Pin_1, TRS1.Ring, TRS1.Tip
  N8: R2.Pin_1, C1.+, R3.Pin_0, R4.Pin_0, TRS1.Sleeve
  N9: R5.Pin_0, R6.Pin_0, C2.+, R7.Pin_0, R8.Pin_0, TRS2.Sleeve
  N10: R9.Pin_0, R10.Pin_0, C3.+, R11.Pin_0, TRS3.Sleeve
  N11: R12.Pin_1, LED1.cathode
  N12: U1.1, U3.SLEEVE
  N13: U1.2, U3.LEFT, U3.RIGHT
  N14: U1.3, JP3.1
  N15: U1.4, JP3.2
  N16: U2.Vin, JP2.4
  N17: U2.GND, JP2.1
  N18: U2.SDA, JP2.3
  N19: U2.SCL, JP2.2
  N20: L2.pin_0, U5.LEFT
  N21: L2.pin_1, U5.SLEEVE
  N22: L1.pin_0, U4.LEFT
  N23: L1.pin_1, U4.SLEEVE

notes:
  220V~
  Sec. 9V~
  Prim. 220V~
  Transformer
  CT 100A

custom parts:
  Adafruit TSL2561: Adafruit TSL2561 Digital Luminosity/Lux/Light Sensor Breakout The TSL2561 luminosity sensor is an advanced digital light sensor, ideal for use in a wide range of light situations. Compared to low cost CdS cells, this sensor is more precise, allowing for exact lux calculations and can be configured for different gain/timing ranges to detect light ranges from up to 0.1 - 40,000+ Lux on the fly.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
